// Logisim project tp6.circ as structural Verilog: 3 circuits, main circuit main
module main (
  input  e,
  output s
);

  wire and_1_out, and_2_out, clock_1_out, not_1_out, not_2_out, not_3_out, or_1_out, or_2_out;

  Clock clock_1 (.out(clock_1_out));
  not not_1 (not_1_out, e);
  and and_1 (and_1_out, clock_1_out, not_1_out);
  and and_2 (and_2_out, clock_1_out, e);
  or or_1 (or_1_out, and_1_out, not_2_out);
  not not_2 (not_2_out, or_2_out);
  or or_2 (or_2_out, not_3_out, and_2_out);
  not not_3 (not_3_out, or_1_out);

  // Notes on the sheet:
  //   h
  //   t
endmodule

module test (
  input  e,
  output s
);

  wire and_1_out, and_2_out, clock_1_out, not_1_out, not_2_out, not_3_out, or_1_out, or_2_out;

  Clock clock_1 (.out(clock_1_out));
  not not_1 (not_1_out, e);
  and and_1 (and_1_out, clock_1_out, not_1_out);
  and and_2 (and_2_out, clock_1_out, e);
  or or_1 (or_1_out, and_1_out, not_2_out);
  not not_2 (not_2_out, or_2_out);
  or or_2 (or_2_out, not_3_out, and_2_out);
  not not_3 (not_3_out, or_1_out);

  // Notes on the sheet:
  //   h
  //   t
endmodule

module verrouD (
  input  e,
  output s
);

  wire and_1_out, and_2_out, clock_1_out, not_1_out, not_2_out, not_3_out, or_1_out, or_2_out;

  Clock clock_1 (.out(clock_1_out));
  not not_1 (not_1_out, e);
  and and_1 (and_1_out, clock_1_out, not_1_out);
  and and_2 (and_2_out, clock_1_out, e);
  or or_1 (or_1_out, and_1_out, not_2_out);
  not not_2 (not_2_out, or_2_out);
  or or_2 (or_2_out, not_3_out, and_2_out);
  not not_3 (not_3_out, or_1_out);

  // Notes on the sheet:
  //   h
  //   t
endmodule
